// Digital circuit main.dig as structural Verilog
module main (
  input  [7:0] Instruction_Binary,
  input  clk,
  input  Write_instruction,
  input  [7:0] Starting_address,
  input  Reset_Program_Counter,
  input  in_7,
  output [7:0] out_2
);

  wire or_1_out;
  wire [7:0] u_counter_8bit_count;

  or or_1 (or_1_out, Write_instruction, in_7);
  counter_8bit #(.applicationType("IVERILOG"), .CodeFile("/home/kaldwin/Development/Projects/the_electronics_project_misc/src/counter_8bit.v")) u_counter_8bit (
    .clk(clk), .num(Starting_address), .load(or_1_out), .reset(Reset_Program_Counter),
    .count(u_counter_8bit_count));
  Instruction_Register #(.applicationType("IVERILOG"), .CodeFile("/home/kaldwin/Development/Projects/the_electronics_project_misc/src/memory_256x8.v")) u_Instruction_Register (
    .clk(clk), .write(Write_instruction), .address(u_counter_8bit_count), .data_in(Instruction_Binary),
    .data_out(out_2));

  // Notes on the sheet:
  //   clk: Hz: 5
endmodule
